# Fritzing sketch HC12Reciever (saved by Fritzing 0.9.3b)
circuit board: 12.7488cm x 9.4737cm
breadboards: 1

parts:
  Arduino_Nano = Arduino Nano (Rev3.0)
  HC-12 = HC-12 Module
  LED1 = RGB LED (com. cathode, rgb) [package="5 mm [THT]"]
  R1 = Resistor [tolerance=±5% resistance=220 package=THT]
  R2 = Resistor [tolerance=±5% resistance=220 package=THT]
  R3 = Resistor [tolerance=±5% resistance=220 package=THT]
  J1 = Basic Servo
  BAT1 = Battery Holders [package=battery-aaa]  # not connected
  SG1 = Buzzer 12mm [package=buzzer-cmt1603]

nets (from the pcb view):
  GND: Arduino_Nano.GND, HC-12.GND, LED1.common_cathode, J1.gnd, SG1.2
  N1: Arduino_Nano.D2, SG1.1
  N2: Arduino_Nano.D3, R1.Pin_0
  N3: Arduino_Nano.D4, R2.Pin_0
  N4: Arduino_Nano.D5, R3.Pin_0
  N5: Arduino_Nano.D8, J1.pulse
  N6: Arduino_Nano.D9, HC-12.TXD
  N7: Arduino_Nano.D10, HC-12.RXD
  VCC: Arduino_Nano.5V, HC-12.VCC, J1.vcc
  N8: LED1.red_anode, R3.Pin_1
  N9: LED1.green_anode, R2.Pin_1
  N10: LED1.blue_anode, R1.Pin_1

custom parts:
  HC-12 Module: HC-12 433Mhz Module
